# Fritzing sketch SmartGlasses (saved by Fritzing 0.9.4)
breadboards: 1
perfboards: 1

parts:
  A1 = Arduino Nano ESP32
  Part1 = Bluetooth HC-06 Macho
  Part2 = KY-037 High Sensitivity Sound Detection Module [package="Breakout board"]
  SP1 = SPEAKER [package=pcb_mount_speaker]
  R1 = Resistor [tolerance=±5% resistance=680 package="0805 [SMD]"]
  R2 = Resistor [tolerance=±5% resistance=1k package="0805 [SMD]"]
  R3 = Resistor [tolerance=±5% resistance=10k package="0805 [SMD]"]
  R4 = Resistor [tolerance=±5% resistance=10k package="0805 [SMD]"]

nets:
  N1: A1.Pin_2, R3.Pin_1
  N2: A1.Pin_8, R3.Pin_0
  N3: A1.Pin_9, R4.Pin_1
  N4: A1.Pin_10, Part2.A0
  N5: A1.Pin_14, A1.Pin_19, Part1.GND, Part2.G, SP1.+, R2.Pin_0
  N6: A1.Pin_15, Part1.VCC, Part2.+
  N7: A1.Pin_16, Part1.TXD
  N8: A1.Pin_17, Part1.RXD
  N9: A1.Pin_21, R1.Pin_1
  N10: A1.Pin_29, SP1.-
  N11: R1.Pin_0, R2.Pin_1

notes:
  BLINK
  D0
  VSYNC
  D4
  D2
  XCLK
  SIOD
  HREF
  PCLK
  GND
  D1
  PWDN
  D5
  RESET
  SIOC
  D3
  + VCC
  D7
  D6

custom parts:
  Arduino Nano ESP32: Arduino® Nano ESP32 smd.
  KY-037 High Sensitivity Sound Detection Module: KY-037 high sensitivity sound detection module is an analog/digital sensor that uses a condenser microphone to observe changes in environment noise.

// code stored in the sketch: Blink.ino
/*
  Blink
  
  Switching a LED on and off
  
  This example is part of the Fritzing Creator Kit: www.fritzing.org/creator-kit.
*/

int led = 13;                   // integer variable led is declared

void setup() {                  // the setup() method is executed only once
  pinMode(led, OUTPUT);         // the led PIN is declared as digital output
}

void loop() {                   // the loop() method is repeated
  digitalWrite(led, HIGH);      // switching on the led 
  delay(1000);                  // stopping the program for 1000 milliseconds
  digitalWrite(led, LOW);       // switching off the led 
  delay(1000);                  // stopping the program for 1000 milliseconds
}
