# Fritzing sketch circuit (saved by Fritzing 0.9.5d)
breadboards: 1

parts:
  BATT1 = LiPoly Battery (1300mAh)
  Part3 = Bluetooth HM-10
  Part4 = INMP441
  A1 = XIAO ESP32C3-tht
  J1 = Piezo Speaker
  J2 = Piezo Speaker

nets:
  N1: BATT1.positive, A1.Pin_8
  N2: BATT1.negative, A1.Pin_7
  N3: Part3.RXD, A1.Pin_15
  N4: Part3.TXD, A1.Pin_14
  N5: Part3.GND, A1.Pin_2, A1.Pin_21, A1.Pin_22, J1.pin1, J2.pin1
  N6: Part3.VCC, A1.Pin_20
  N7: Part4.L/R, Part4.GND
  N8: Part4.WS, Part4.VDD, A1.Pin_13
  N9: Part4.SCK, Part4.SD, A1.Pin_11, A1.Pin_12
  N10: A1.Pin_16, J1.pin2, J2.pin2

custom parts:
  LiPoly Battery (1300mAh): Lithium Ion Polymer Battery (1300mAh)
  INMP441: This is a simple breakout board for the INMP441 I2S MEMS microphone.
  XIAO ESP32C3-tht: Seeed Studio XIAO ESP32C3 adopts new RISC-V architecture, supporting both Wi-Fi and BLE wireless connectivities.
